# Fritzing sketch ECM (saved by Fritzing 0.9.3b)

parts:
  U1 = ESP32-38PinWide [part_number=ESP32-38PinWide]
  L298N1 = L298N DC motor driver
  U2 = LM2596 step down module
  Part1 = Adafruit ADS1115 16Bit I2C ADC [part_number="Adafruit #1085"]
  TPS_Connector_(ECM) = Generic double row male header - 6 pins [form="♂ (male)" package=THT]
  TPS_Connector_(TPS) = Generic double row male header - 6 pins [form="♂ (male)" package=THT]
  APPS_Connector = Generic double row male header - 6 pins [form="♂ (male)" package=THT]
  5v_Power_Splice = female pin header, 2 pins [form="♀ (female)"]
  Power_Connector = double row male pin header, 4 pins [form="♂ (male)"]
  Power_Connector_2 = double row male pin header, 4 pins [form="♂ (male)"]
  Battery_Connector = double row male pin header, 4 pins [form="♂ (male)"]
  J1 = female pin header, 2 pins [form="♀ (female)"]
  BAT1 = 12 battery [package=battery]

nets:
  N1: U1.GPIO26, L298N1.IN2
  N2: U1.GPIO27, L298N1.IN1
  N3: U1.GPIO14, L298N1.5V, L298N1.ENA
  GND: U1.GPIO11, L298N1.GND, U2.IN-, U2.OUT-, Part1.GND, APPS_Connector.gnd, 5v_Power_Splice.pin1, Power_Connector.pin2, Power_Connector.pin4, Power_Connector_2.pin1, Power_Connector_2.pin3, Battery_Connector.pin1, Battery_Connector.pin3, J1.pin1, BAT1.-
  VIN: U1.VIN, U2.OUT+, Part1.VDD, APPS_Connector.5v, 5v_Power_Splice.pin2, Power_Connector.pin1, Power_Connector.pin3, Power_Connector_2.pin2, Power_Connector_2.pin4
  N4: U1.GPIO21, Part1.SDA
  N5: U1.GPIO22, Part1.SCL
  N6: L298N1.OUT1, TPS_Connector_(TPS).motor_const
  N7: L298N1.OUT2, TPS_Connector_(TPS).motor_pwm
  N8: L298N1.12V, U2.IN+, Battery_Connector.pin2, Battery_Connector.pin4, J1.pin2, BAT1.+
  N9: Part1.AIN1, APPS_Connector.apps_2
  N10: Part1.AIN0, APPS_Connector.apps_1
  5V: TPS_Connector_(ECM).5v, TPS_Connector_(TPS).5v
  GND_2: TPS_Connector_(ECM).gnd, TPS_Connector_(TPS).gnd
  N11: TPS_Connector_(ECM).tps_1, TPS_Connector_(TPS).tps_1
  N12: TPS_Connector_(ECM).tps_2, TPS_Connector_(TPS).tps_2

notes:
  tps 2 splice
  tps 1 splice

custom parts:
  ESP32-38PinWide: Generic 38-Pin ESP32 with wide format (only access to one side of pins on a breadboard) based on Stephen Lilley's HiLetgo ESP-WROOM-32 ESP32 ESP-32S Development Board.
  L298N DC motor driver: 2x DC motor driver with 78M05 positive voltage regulator (7..35 V) L298N: max 46 V, 2 A Set 5 V Enable jumper to enable 5 V regultor (needed for the L298N) and +5 V output at screw terminal or supply external +5 V at screw terminal Set ENA and/or ENB to +5 V to enable motor permanently or supply ENA and/or ENB with PWM signal IN1 and IN2 set rotation directory for motor A (OUT1/OUT2) IN2 and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
  LM2596 step down module: LM2596 DC-DC step down power supply module 3 A.
  Adafruit ADS1115 16Bit I2C ADC: For microcontrollers without an analog-to-digital converter or when you want a higher-precision ADC, the ADS1115 provides 16-bit precision at 860 samples/second over I2C. The chip can be configured as 4 single-ended input channels, or two differential channels. As a nice bonus, it even includes a programmable gain amplifier, up to x16, to help boost up smaller single/differential signals to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
  Generic double row male header - 6 pins: Generic double row male header
  Generic double row male header - 6 pins: Generic double row male header
  12 battery: 12V lead acid type battery, like the Husqvarna YTH2448 12V 35AH battery. This is the mini version 1/4 the size of the actual battery to be closer to typical breadboard parts (around 2in wide rathher than 7in). The pads in pcb are sized to accomidate up to 14ga wire (as these batterys will deliver high currents.)
